# Fritzing sketch assignment1_interaction_Technology (saved by Fritzing 0.9.3b)
breadboards: 1

parts:
  U1 = lolin
  R1 = Temperature Sensor (Thermistor) [thermistor_type=NTC package=THT]
  R2 = Photocell (LDR) [package=THT]
  R3 = Resistor [tolerance=±5% resistance=100k package="0402 [SMD]"]
  Part1 = Breakout Board for Electret Microphone
  LED1 = LED - 3mm [color="Red (635nm)" package="3 mm [THT]"]
  LED2 = LED - 3mm [color="Yellow (592nm)" package="3 mm [THT]"]
  LED3 = LED - 3mm [color="Green (555nm)" package="3 mm [THT]"]
  R7 = Resistor [tolerance=±5% resistance=220 package="0402 [SMD]"]
  R8 = Resistor [tolerance=±5% resistance=220 package="0402 [SMD]"]
  R9 = Resistor [tolerance=±5% resistance=220 package="0402 [SMD]"]
  R10 = Resistor [tolerance=±5% resistance=10k package="0402 [SMD]"]
  DHT1 = DHT22 Humidity and Temperature Sensor
  R11 = Resistor [tolerance=±5% resistance=10k package="0402 [SMD]"]

nets:
  N1: U1.connector0, U1.connector1, R1.pin_1, R2.pin_0, R3.Pin_1, Part1.AUD, DHT1.VDD, R11.Pin_1
  N2: U1.connector5, Part1.VCC
  N3: U1.connector8, LED2.anode
  N4: U1.connector10, R1.pin_0, R3.Pin_0
  N5: U1.connector11, R2.pin_1, R10.Pin_0
  N6: U1.connector12, LED1.anode
  N7: U1.connector13, LED3.anode
  GND: U1.connector14, U1.connector15, Part1.GND, R7.Pin_1, R8.Pin_1, R9.Pin_1, R10.Pin_1, DHT1.GND
  N8: U1.connector33, DHT1.DATA, R11.Pin_0
  N9: LED1.cathode, R7.Pin_0
  N10: LED2.cathode, R8.Pin_0
  N11: LED3.cathode, R9.Pin_0
