# Fritzing sketch project (saved by Fritzing 0.9.3b)
breadboards: 1

parts:
  U1 = lolin
  hc-sr1 = hc-sr04
  D2 = Schottky Diode [part_number=1N5817 package="300 mil [THT]"]
  D3 = Schottky Diode [part_number=1N5817 package="300 mil [THT]"]
  Q1 = NPN-Transistor [package="TO92 [THT]"]
  Q2 = NPN-Transistor [package="TO92 [THT]"]
  Keyes2 = Keyes IR Infrared Sensor Switch Module
  Keyes3 = Keyes IR Infrared Sensor Switch Module
  M3 = DC Motor
  M4 = DC Motor
  R3 = Resistor [tolerance=±5% resistance=220 package="0805 [SMD]"]
  R2 = Resistor [tolerance=±5% resistance=220 package="0805 [SMD]"]

nets:
  N1: U1.connector4, hc-sr1.Echo
  N2: U1.connector5, hc-sr1.Trig
  N3: U1.connector8, R3.Pin_0
  N4: U1.connector9, R2.Pin_0
  N5: U1.connector11, Keyes3.connector3
  N6: U1.connector14, hc-sr1.VCC, D2.cathode, D3.cathode, Keyes2.connector1, Keyes3.connector1, M3.pin_2, M4.pin_2
  N7: U1.connector15, hc-sr1.GND, Q2.C, Keyes3.connector0
  N8: U1.connector23, Keyes2.connector3
  N9: U1.connector37, Q1.C, Keyes2.connector0
  N10: D2.anode, Q2.E, M4.pin_1
  N11: D3.anode, Q1.E, M3.pin_1
  N12: Q1.B, R3.Pin_1
  N13: Q2.B, R2.Pin_1
